# Fritzing sketch Verbindung (saved by Fritzing 0.9.3b)
perfboards: 1

parts:
  JACK1 = 2.1mm Barrel Jack with Terminal Block
  VALVE1 = Plastic Solenoid Valve
  Mod1 = KY-019 5V Relay Module [package="Breakout board"]
  U1 = ATTINY45 [package=dip]
  RXB1 = RXB14
  D1 = Schottky Diode [part_number=1N5817 package="Melf DO-213 AB [SMD]"]
  C1 = Electrolytic Capacitor [capacitance=10µF voltage=5 package="200 mil [THT, electrolytic]"]
  LED1 = LED - 5mm [color="Green (565nm)" package="5 mm [THT]"]
  R1 = Resistor [tolerance=±5% resistance=150 package=THT]
  JACK2 = 2.1mm Barrel Jack with Terminal Block
  JACK3 = 2.1mm Barrel Jack with Terminal Block
  U2 = Mini-360 DC-DC Buck converter [package=THT]

nets:
  N1: JACK1.POS, Mod1.Common, C1.+, U2.IN+
  N2: JACK1.NEG, C1.-, JACK2.NEG, U2.IN-
  N3: VALVE1.no_name_yet#1, D1.anode, JACK3.NEG
  N4: VALVE1.no_name_yet#2, D1.cathode, JACK3.POS
  N5: Mod1.S, U1.PB3(ADC3)
  N6: Mod1.+, U2.OUT+
  N7: Mod1.NO, JACK2.POS
  N8: U1.PB0(MOSI), R1.Pin_0
  N9: U1.PB1(MISO), RXB1.pin_2
  N10: LED1.anode, R1.Pin_1

custom parts:
  KY-019 5V Relay Module: KY-019 5V Relay module, used to control AC circuits. (Special thanks to vanepp for fixing the PCB holes and other errors)
  RXB14: RXB14 433mhz Empfangsmodul
  Mini-360 DC-DC Buck converter: Mini-360 DC-DC Buck converter. Tiny buck step down voltage converter, input voltage 4.75 to 23V output 1 to 17V adjustable. Available from ebay and the like.
